# Fritzing sketch Full_System (saved by Fritzing 0.9.3b)
breadboards: 1

parts:
  Part2 = Adafruit HUZZAH32 ESP32 Feather [part_number="Adafruit #3405"]
  OLED2 = OLED 128x64 I2C Monochrome Display
  Part3 = Adafruit TCS34725 RGB Color Sensor [part_number="Adafruit #1334"]
  DRV_1 = DRV 8825 Stepper Motor Carrier, High Current [part_number="DRV 8825"]  # not connected
  M2 = Stepper Motor - Bipolar  # not connected
  C1 = Electrolytic Capacitor [capacitance=100μF package="0807 [SMD, electrolytic]"]
  J1 = Power Jack [package=power_jack_slot]

nets:
  GND: Part2.GND, OLED2.GND, Part3.GND
  3.3V: Part2.3.3V, Part3.+3V3
  N1: Part2.VBUS, OLED2.VDD
  N2: Part2.SCL, OLED2.SCK, Part3.SCL
  N3: Part2.SDA, OLED2.SDA, Part3.SDA
  N4: C1.-, J1.PWR
  N5: C1.+, J1.GND

custom parts:
  Adafruit TCS34725 RGB Color Sensor: Your electronics can now see in dazzling color with this lovely color light sensor. We found the best color sensor on the market, the TCS34725, which has RGB and Clear light sensing elements. An IR blocking filter, integrated on-chip and localized to the color sensing photodiodes, minimizes the IR spectral component of the incoming light and allows color measurements to be made accurately. The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
