# Fritzing sketch Oled Sketch (saved by Fritzing 0.9.3b)
breadboards: 1

parts:
  Part1 = Adafruit HUZZAH32 ESP32 Feather [part_number="Adafruit #3405"]
  OLED1 = OLED 128x64 I2C Monochrome Display
  R1 = Resistor [tolerance=±5% resistance=220 package="0805 [SMD]"]
  LED1 = LEDs [package=led10mm]

nets:
  GND: Part1.GND, OLED1.GND, R1.Pin_1
  N1: Part1.VBUS, OLED1.VDD
  N2: Part1.IO14_A6, R1.Pin_0, LED1.C, LED1.A
  N3: Part1.SCL, OLED1.SCK
  N4: Part1.SDA, OLED1.SDA
