# Fritzing sketch Full_System (remodeled) (saved by Fritzing 0.9.3b)
breadboards: 2

parts:
  Part1 = Adafruit HUZZAH32 ESP32 Feather [part_number="Adafruit #3405"]
  DRV_2 = DRV 8825 Stepper Motor Carrier, High Current [part_number="DRV 8825"]  # not connected
  DRV_3 = DRV 8825 Stepper Motor Carrier, High Current [part_number="DRV 8825"]  # not connected
  M3 = Stepper Motor - Bipolar  # not connected
  M4 = Stepper Motor - Bipolar  # not connected
  J2 = Power Jack [package=power_jack_slot]
  C2 = Electrolytic Capacitor [capacitance=100μF package="0807 [SMD, electrolytic]"]
  C3 = Electrolytic Capacitor [capacitance=100μF package="0807 [SMD, electrolytic]"]
  U3 = 2-Channel 5v Relay Shield [package=relay-2ch5v10a]
  M6 = RioRand LM2596
  LED3 = DUO LED RG [package="5 mm [THT]"]
  OLED3 = OLED 128x64 I2C Monochrome Display
  U4 = 2-Channel 5v Relay Shield [package=relay-2ch5v10a]
  Part4 = Adafruit TCS34725 RGB Color Sensor [part_number="Adafruit #1334"]
  LED4 = LEDs [package=led10mm]
  LED5 = LEDs [package=led10mm]
  R1 = Resistor [tolerance=±5% resistance=220 package="0805 [SMD]"]
  R2 = Resistor [tolerance=±5% resistance=220 package="0805 [SMD]"]
  R3 = Temperature Sensor (Thermistor) [thermistor_type=NTC package=THT]
  R4 = Resistor [tolerance=±5% resistance=220 package=THT]
  T3 = LM34 Temperature Sensor [package="TO92 [THT]"]

nets:
  N1: Part1.A2_I34, T3.Vout
  N2: Part1.A1_DAC1, U3.IN1
  N3: Part1.A0_DAC2, U3.IN2
  GND: Part1.GND, U3.GND, OLED3.GND, U4.GND, Part4.GND, LED4.C, LED5.C, R3.pin_1, T3.GND
  VCC: Part1.3.3V, U3.VCC, OLED3.VDD, U4.VCC, Part4.+3V3, R1.Pin_1, R2.Pin_1, R4.Pin_0, T3.+Vs
  N4: Part1.IO12_A11, U4.IN1
  N5: Part1.IO27_A10, U4.IN2
  N6: Part1.IO32_A7, R3.pin_0, R4.Pin_1
  N7: Part1.SCL, OLED3.SCK, Part4.SCL
  N8: Part1.SDA, OLED3.SDA, Part4.SDA
  N9: J2.GNDBREAK, C2.-, C3.-, U3.JD-GND, M6.Pin_2
  N10: J2.GND, C2.+, C3.+
  N11: J2.PWR, M6.Pin_1
  N12: U3.K1-In, LED3.red_anode
  N13: U3.K1-On, U3.K2-On, M6.Pin_4
  N14: U3.K2-In, LED3.common_cathode
  N15: M6.Pin_3, LED3.green_anode
  N16: LED4.A, R2.Pin_0
  N17: LED5.A, R1.Pin_0

custom parts:
  2-Channel 5v Relay Shield: 2 Channel 5v Relay Shield w. 2x SPD-06VDC-SD-C
  Adafruit TCS34725 RGB Color Sensor: Your electronics can now see in dazzling color with this lovely color light sensor. We found the best color sensor on the market, the TCS34725, which has RGB and Clear light sensing elements. An IR blocking filter, integrated on-chip and localized to the color sensing photodiodes, minimizes the IR spectral component of the incoming light and allows color measurements to be made accurately. The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
