# Fritzing sketch Lamp (saved by Fritzing 0.9.3b)
breadboards: 1

parts:
  U1 = 2-Channel 5v Relay Shield [package=relay-2ch5v10a]
  M4 = RioRand LM2596
  Part1 = Adafruit HUZZAH32 ESP32 Feather [part_number="Adafruit #3405"]
  LED1 = DUO LED RG [package="5 mm [THT]"]

nets:
  VCC: U1.VCC, Part1.3.3V
  GND: U1.GND, Part1.GND
  N1: U1.IN1, Part1.A1_DAC1
  N2: U1.IN2, Part1.A0_DAC2
  N3: U1.K1-In, LED1.red_anode
  N4: U1.K1-On, U1.K2-On, M4.Pin_4
  N5: U1.K2-In, LED1.common_cathode
  N6: U1.JD-GND, M4.Pin_2
  N7: M4.Pin_3, LED1.green_anode

custom parts:
  2-Channel 5v Relay Shield: 2 Channel 5v Relay Shield w. 2x SPD-06VDC-SD-C
